# Fritzing sketch schematic (saved by Fritzing 0.9.10b)
breadboards: 1

parts:
  Part2 = Arduino Nano (Rev3.0)
  DATA_0_OUT = female pin header, 1 pin [form="♀ (female)"]
  DATA_1_OUT = female pin header, 1 pin [form="♀ (female)"]
  DATA_2_OUT = female pin header, 1 pin [form="♀ (female)"]
  DATA_3_OUT = female pin header, 1 pin [form="♀ (female)"]
  DATA_4_OUT = female pin header, 1 pin [form="♀ (female)"]
  DATA_5_OUT = female pin header, 1 pin [form="♀ (female)"]
  DATA_6_OUT = female pin header, 1 pin [form="♀ (female)"]
  DATA_7_OUT = female pin header, 1 pin [form="♀ (female)"]
  INTERRUPT_OUT = female pin header, 1 pin [form="♀ (female)"]
  ADDR_0_OUT = female pin header, 1 pin [form="♀ (female)"]
  ADDR_1_OUT = female pin header, 1 pin [form="♀ (female)"]

nets:
  GND: Part2.GND
  N1: Part2.D2, INTERRUPT_OUT.pin1
  N2: Part2.D3, ADDR_0_OUT.pin1
  N3: Part2.D4, ADDR_1_OUT.pin1
  N4: Part2.D5, DATA_0_OUT.pin1
  N5: Part2.D6, DATA_1_OUT.pin1
  N6: Part2.D7, DATA_2_OUT.pin1
  N7: Part2.D8, DATA_3_OUT.pin1
  N8: Part2.D9, DATA_4_OUT.pin1
  N9: Part2.D10, DATA_5_OUT.pin1
  N10: Part2.D11/MOSI, DATA_6_OUT.pin1
  N11: Part2.D12/MISO, DATA_7_OUT.pin1
  5V: Part2.5V
